// Logisim project Koyaanisqatsi-combo.circ as structural Verilog: 1 circuit, main circuit main
module main (
  output [7:0] Instruction_Code
);

  wire and_1_out, and_2_out, and_3_out, and_4_out, and_5_out, and_6_out, and_7_out, and_8_out, and_9_out,
       and_10_out, and_11_out, clock_1_out, decoder_1_out2, decoder_1_out3, decoder_1_out4, decoder_1_out5,
       decoder_1_out6, nand_1_out, nand_2_out, nand_3_out, Next_out, nor_1_out, nor_2_out, nor_3_out,
       not_1_out, not_2_out, not_3_out, or_1_out, or_2_out, or_3_out, TICK, xor_2_out, xor_3_out;
  wire [3:0] register_3_q;
  wire [7:0] register_1_q, register_2_q;

  Clock clock_1 (.out(clock_1_out));
  Button Next (.out(Next_out));
  Counter #(.trigger("falling")) counter_1 (
    .count(1'b1), .Q(Instruction_Code), .clk(TICK));  // open: load, D, carry, clr
  xor xor_1 (TICK, clock_1_out, Next_out);
  Hex_Digit_Display hex_digit_display_1 (.value(Instruction_Code[7:4]));  // open: dp
  Hex_Digit_Display hex_digit_display_2 (.value(Instruction_Code[3:0]));  // open: dp
  or or_1 (or_1_out, Instruction_Code[5], Instruction_Code[6]);
  xor xor_2 (xor_2_out, Instruction_Code[5], Instruction_Code[6]);
  or or_2 (or_2_out, Instruction_Code[1], Instruction_Code[2]);
  xor xor_3 (xor_3_out, Instruction_Code[1], Instruction_Code[2]);
  not not_1 (not_1_out, Instruction_Code[0]);
  not not_2 (not_2_out, Instruction_Code[4]);
  or or_3 (or_3_out, Instruction_Code[1], Instruction_Code[2], Instruction_Code[3]);
  nor nor_1 (nor_1_out, Instruction_Code[4], Instruction_Code[5], Instruction_Code[6], Instruction_Code[7]);
  nor nor_2 (nor_2_out, Instruction_Code[0], Instruction_Code[1], Instruction_Code[2], Instruction_Code[3]);
  LED _0___9 (.in(nand_1_out));
  LED A___D (.in(and_2_out));
  and and_1 (and_1_out, and_2_out, nand_2_out);
  nand nand_1 (nand_1_out, or_1_out, Instruction_Code[7]);
  and and_2 (and_2_out, xor_2_out, Instruction_Code[7]);
  and and_3 (and_3_out, nand_1_out, or_2_out, Instruction_Code[3]);
  nand nand_2 (nand_2_out, or_2_out, Instruction_Code[3]);
  and and_4 (and_4_out, xor_3_out, Instruction_Code[3]);
  and and_5 (and_5_out, and_4_out, and_2_out);
  and and_6 (and_6_out, and_2_out, not_1_out, Instruction_Code[1], Instruction_Code[2], Instruction_Code[3]);
  and and_7 (and_7_out, and_2_out, Instruction_Code[0], Instruction_Code[1], Instruction_Code[2], Instruction_Code[3]);
  and and_8 (and_8_out, not_2_out, Instruction_Code[3], Instruction_Code[5], Instruction_Code[6], Instruction_Code[7]);
  and and_9 (and_9_out, nand_2_out, or_3_out, nor_1_out);
  not not_3 (not_3_out, and_9_out);
  nand nand_3 (nand_3_out, nor_1_out, nor_2_out);
  and and_10 (and_10_out, nor_2_out, Instruction_Code[4], Instruction_Code[5], Instruction_Code[6], Instruction_Code[7]);
  LED _0___9_2 (.in(nand_2_out));
  LED A___D_2 (.in(and_4_out));
  LED _00__E0__E7__F1__FF___CALL (.in(nor_3_out));
  LED An__Dn___Rn (.in(and_1_out));
  LED nA__nF___ALU (.in(and_3_out));
  LED AA__DD___Ri_Tj (.in(and_5_out));
  LED AE__DE___EXT_Ri (.in(and_6_out));
  LED AF__DF___FIX_Ri (.in(and_7_out));
  LED E8__EF___Ecnd (.in(and_8_out));
  LED _02__09___REP_n (.in(and_9_out));
  LED F0___FO (.in(and_10_out));
  LED _01__99___BCD (.in(and_11_out));
  Decoder #(.select(3), .disabled(0)) decoder_1 (
    .out2(decoder_1_out2), .out3(decoder_1_out3), .out4(decoder_1_out4), .out5(decoder_1_out5),
    .out6(decoder_1_out6), .sel(Instruction_Code[2:0]), .en(and_3_out));  // open: out0, out1, out7
  nor nor_3 (nor_3_out, and_11_out, and_8_out, and_1_out, and_3_out, and_5_out, and_6_out, and_7_out, and_9_out, and_10_out);
  and and_11 (and_11_out, nand_1_out, not_3_out, nand_2_out, nand_3_out);
  LED ADD (.in(decoder_1_out2));
  LED SUB (.in(decoder_1_out3));
  LED AND_12 (.in(decoder_1_out4));
  LED OR_4 (.in(decoder_1_out5));
  LED EOR (.in(decoder_1_out6));
  Hex_Digit_Display hex_digit_display_3 (.value(register_1_q[7:4]));  // open: dp
  Register register_1 (.D(Instruction_Code), .en(and_1_out), .Q(register_1_q), .clk(TICK));  // open: clr
  Hex_Digit_Display hex_digit_display_4 (.value(register_2_q[7:4]));  // open: dp
  Register register_2 (.D(Instruction_Code), .en(and_5_out), .Q(register_2_q), .clk(TICK));  // open: clr
  Hex_Digit_Display hex_digit_display_5 (.value(register_1_q[3:0]));  // open: dp
  Hex_Digit_Display hex_digit_display_6 (.value(register_1_q[3:0]));  // open: dp
  Hex_Digit_Display hex_digit_display_7 (.value(register_2_q[3:0]));  // open: dp
  Register #(.width(4)) register_3 (
    .D(Instruction_Code[7:4]), .en(and_3_out), .Q(register_3_q), .clk(TICK));  // open: clr
  Hex_Digit_Display hex_digit_display_8 (.value(register_3_q));  // open: dp

  // Other names for the same wires on the sheet: CODE[7:0] = Instruction_Code; LOW[3:0] = Instruction_Code[3:0];
  //   HIGH[3:0] = Instruction_Code[7:4]

  // Notes on the sheet:
  //   https://github.com/Alikberov/Koyaanisqatsi
endmodule
