// Logisim project Koyaanisqatsi.circ as structural Verilog: 1 circuit, main circuit main
module main (
  input  BIT_4,
  input  BIT_5,
  input  BIT_6,
  input  BIT_7,
  input  CLK,
  input  WAIT
);

  wire adder_1_cout, and_1_out, and_2_out, and_3_out, and_4_out, and_5_out, and_6_out, and_7_out, and_8_out,
       and_9_out, and_10_out, and_12_out, and_13_out, and_14_out, and_16_out, and_17_out, and_18_out,
       and_19_out, and_21_out, and_22_out, and_23_out, and_24_out, and_25_out, and_26_out, and_27_out,
       and_28_out, and_29_out, and_30_out, and_31_out, and_32_out, and_33_out, and_34_out, and_35_out,
       and_36_out, and_37_out, and_38_out, and_39_out, and_40_out, and_41_out, and_42_out, and_43_out,
       and_44_out, and_45_out, and_46_out, and_47_out, and_48_out, and_49_out, and_50_out, and_51_out,
       and_52_out, and_53_out, and_54_out, and_55_out, and_56_out, and_57_out, and_58_out, and_59_out,
       and_60_out, BIT_4_out, BIT_5_out, BIT_6_out, BIT_7_out, CLK_t, clock_1_out, counter_1_carry,
       counter_2_carry, d_ff_1_qn, d_ff_2_q, decoder_1_out0, decoder_1_out1, decoder_1_out2, decoder_1_out3,
       decoder_1_out4, decoder_1_out5, decoder_1_out6, decoder_1_out8, decoder_1_out9, decoder_1_out10,
       decoder_1_out11, decoder_1_out12, decoder_1_out13, decoder_1_out14, decoder_1_out15, decoder_2_out0,
       decoder_2_out1, decoder_2_out2, decoder_2_out3, decoder_3_out0, decoder_3_out1, decoder_3_out2,
       decoder_3_out3, decoder_4_out1, decoder_5_out0, decoder_5_out1, decoder_5_out2, decoder_5_out3,
       decoder_5_out4, decoder_5_out5, decoder_5_out6, decoder_5_out7, decoder_5_out8, decoder_5_out9,
       decoder_6_out0, decoder_6_out1, decoder_6_out2, decoder_6_out3, decoder_6_out4, decoder_6_out5,
       decoder_6_out6, decoder_6_out7, decoder_6_out8, decoder_6_out9, decoder_7_out0, decoder_7_out1,
       decoder_7_out2, decoder_7_out3, decoder_7_out4, decoder_7_out5, decoder_7_out6, decoder_7_out7,
       decoder_7_out8, decoder_7_out9, decoder_8_out0, decoder_8_out1, decoder_8_out2, decoder_8_out3,
       decoder_8_out4, decoder_8_out5, decoder_8_out6, decoder_8_out7, decoder_8_out8, decoder_8_out9,
       decoder_10_out0, decoder_10_out1, decoder_10_out2, decoder_10_out3, decoder_10_out4, decoder_10_out5,
       decoder_10_out6, decoder_10_out7, decoder_10_out8, decoder_10_out9, decoder_11_out0, decoder_11_out1,
       decoder_11_out2, decoder_11_out3, decoder_11_out4, decoder_11_out5, decoder_11_out6, decoder_11_out7,
       decoder_11_out8, decoder_11_out9, decoder_12_out0, decoder_12_out1, decoder_12_out2, decoder_12_out3,
       decoder_12_out4, decoder_12_out5, decoder_12_out6, decoder_12_out7, decoder_12_out8, decoder_12_out9,
       decoder_13_out0, decoder_13_out1, decoder_13_out2, decoder_13_out3, decoder_13_out4, decoder_13_out5,
       decoder_13_out6, decoder_13_out7, decoder_13_out8, decoder_13_out9, keyboard_1_avail, M1,
       multiplexer_5_out, nand_1_out, nor_1_out, nor_3_out, nor_5_out, nor_7_out, not_1_out, not_2_out,
       not_3_out, not_5_out, not_6_out, not_7_out, not_8_out, not_9_out, or_1_out, or_2_out, or_3_out,
       or_4_out, or_5_out, or_6_out, or_7_out, or_9_out, or_10_out, or_11_out, or_12_out, or_13_out,
       or_16_out, or_17_out, or_18_out, or_19_out, or_20_out, or_21_out, or_22_out, or_23_out, RAM, RD,
       RESET_out, s_r_ff_1_qn, shift_register_1_q1, shift_register_1_q2, shift_register_1_q3,
       subtractor_1_bout, TICK_out, WR;
  wire [1:0] multiplexer_6_out, multiplexer_7_out, or_8_out, R_T_2_q, R_T_2_q_2;
  wire [2:0] controlled_buffer_1_out_2;
  wire [3:0] A0_q, A0_q_2, and_20_out, C0_q, C0_q_2, controlled_buffer_1_out, controlled_buffer_9_out,
       controlled_buffer_9_out_2, counter_1_q, counter_2_q, counter_3_q, counter_4_q, joystick_1_x,
       joystick_1_y, multiplexer_8_out, multiplexer_10_out, multiplexer_12_out, multiplexer_14_out,
       nor_6_out, register_1_q_2, register_3_q, register_4_q, register_5_q, register_6_q, xor_4_out;
  wire [3:3] nor_2_out;
  wire [7:0] A1_q, A2_q, A3_2_q, A3_q, A4_q, A5_q, A6_q, A7_q, A8_q, A9_q, adder_1_out, and_15_out,
       and_61_out, B0_q, B1_q, B2_q, B3_q, B4_q, B5_q, B6_q, B7_q, B8_q, B9_q, C1_q, C2_q, C4_q, C5_q, C6_q,
       C7_q, C8_q, C9_q, controlled_buffer_10_out, controlled_buffer_11_out, controlled_buffer_14_out,
       controlled_buffer_15_out, controlled_buffer_16_out, D0_q, D1_q, D8_q, D9_q, DATA, IC, IP_q, IP_q_2,
       keyboard_1_data, multiplexer_1_out, multiplexer_2_out, multiplexer_9_out, multiplexer_11_out,
       multiplexer_13_out, multiplexer_15_out, multiplexer_16_out, not_4_out, or_14_out, register_1_q,
       rom_1_data, shifter_1_out, subtractor_1_out, undriven, undriven_2, xor_2_out;
  wire [7:7] decoder_1_out7;
  wire [15:0] ADDR, decoder_9_out0, decoder_14_out15, multiplexer_3_out, PTR;

  Counter #(.width(4), .max('h9)) counter_1 (
    .Q(counter_1_q), .carry(counter_1_carry), .clk(CLK_t), .clr(nor_1_out));  // open: load, D, count
  LED E0 (.in(decoder_1_out0));
  LED _00___E0__E7___F0__FF (.in(decoder_1_out1));
  LED REP (.in(decoder_1_out2));
  LED R_T (.in(decoder_1_out3));
  LED _4 (.in(decoder_1_out4));
  LED _5 (.in(decoder_1_out5));
  LED LD (.in(decoder_1_out6));
  LED ST (.in(decoder_1_out7[7]));
  LED E8__EF (.in(decoder_1_out8));
  LED R0__R9 (.in(decoder_1_out9));
  LED ADD_Ri_Tn (.in(decoder_1_out10));
  LED SUB_Ri_Tn (.in(decoder_1_out11));
  LED AND_Ri_Tn (.in(decoder_1_out12));
  LED OR_Ri_Tn (.in(decoder_1_out13));
  LED EOR_Ri_Tn (.in(decoder_1_out14));
  LED F (.in(decoder_1_out15));
  Counter #(.width(4), .max('h9)) counter_2 (
    .count(counter_1_carry), .Q(counter_2_q), .carry(counter_2_carry), .clk(CLK_t), .clr(nor_1_out));  // open: load, D
  nor nor_1 (nor_1_out, IC[0], IC[1], IC[2], IC[3], IC[4], IC[5], IC[6], IC[7]);
  ROM rom_1 (.addr(IC), .data(rom_1_data));  // open: sel
  and and_1 (and_1_out, counter_1_carry, counter_2_carry);
  Counter #(.width(4), .max('h9)) counter_3 (
    .count(and_1_out), .Q(counter_3_q), .clk(CLK_t), .clr(nor_1_out));  // open: load, D, carry
  Hex_Digit_Display hex_digit_display_1 (.value(counter_3_q));  // open: dp
  S_R_Flip_Flop s_r_ff_1 (.S(and_5_out), .clk(CLK_t), .R(M1), .Qn(s_r_ff_1_qn));  // open: Q, preset, reset, en
  Hex_Digit_Display hex_digit_display_2 (.value(counter_1_q));  // open: dp
  Hex_Digit_Display hex_digit_display_3 (.value(counter_2_q));  // open: dp
  and and_2 (and_2_out, rom_1_data[4], rom_1_data[5], nor_7_out, rom_1_data[6], ~rom_1_data[7]);  // AND_Gate
  not not_1 (not_1_out, and_2_out);
  Decoder #(.select(4), .disabled(0)) decoder_1 (
    .out0(decoder_1_out0), .out1(decoder_1_out1), .out2(decoder_1_out2), .out3(decoder_1_out3),
    .out4(decoder_1_out4), .out5(decoder_1_out5), .out6(decoder_1_out6), .out7(decoder_1_out7[7]),
    .out8(decoder_1_out8), .out9(decoder_1_out9), .out10(decoder_1_out10), .out11(decoder_1_out11),
    .out12(decoder_1_out12), .out13(decoder_1_out13), .out14(decoder_1_out14), .out15(decoder_1_out15),
    .sel(rom_1_data[3:0]), .en(and_2_out));
  and and_3 (and_3_out, not_1_out, nor_7_out);
  or or_1 (or_1_out, decoder_1_out6, decoder_1_out7[7]);
  or or_2 (or_2_out, and_4_out, and_3_out, or_4_out);
  and and_4 (and_4_out, decoder_1_out6, shift_register_1_q3);
  LED u_M1 (.in(M1));
  LED Mx (.in(and_18_out));
  LED M2 (.in(shift_register_1_q1));
  or or_3 (or_3_out, decoder_1_out0, decoder_1_out1);
  and and_5 (and_5_out, or_3_out, s_r_ff_1_qn);
  and and_6 (and_6_out, d_ff_2_q, decoder_1_out8);
  Hex_Digit_Display hex_digit_display_4 (.value(register_1_q_2));  // open: dp
  Hex_Digit_Display hex_digit_display_5 (.value(register_1_q[7:4]));  // open: dp
  Register #(.width(12)) register_1 (
    .D({counter_3_q, counter_2_q, counter_1_q}), .Q({register_1_q_2, register_1_q}), .clk(nor_1_out));  // open: en, clr
  Multiplexer #(.width(8), .disabled(0), .enable("false")) multiplexer_1 (
    .in0(multiplexer_16_out), .in1(rom_1_data), .out(multiplexer_1_out), .sel(not_1_out));
  or or_4 (or_4_out, decoder_1_out10, decoder_1_out11, decoder_1_out12, decoder_1_out13, decoder_1_out14, decoder_1_out15);
  LED M4 (.in(shift_register_1_q3));
  LED M3 (.in(shift_register_1_q2));
  LED CND (.in(d_ff_2_q));
  LED REP_2 (.in(or_17_out));
  LED u_WR (.in(decoder_1_out7[7]));
  or or_5 (or_5_out, decoder_1_out0, d_ff_2_q);
  not not_2 (not_2_out, WAIT);
  nor nor_2 (nor_2_out[3], decoder_1_out1, or_12_out);
  Hex_Digit_Display hex_digit_display_6 (.value(register_1_q[3:0]));  // open: dp
  assign {nor_6_out[3], controlled_buffer_1_out_2, controlled_buffer_1_out} = or_6_out ? adder_1_out : 8'bz;  // Controlled_Buffer controlled_buffer_1
  Adder adder_1 (.a(multiplexer_15_out), .b(multiplexer_1_out), .out(adder_1_out), .cin(A0_q[1]), .cout(adder_1_cout));
  or or_6 (or_6_out, decoder_1_out10, and_3_out);
  not not_3 (not_3_out, and_7_out);
  and and_7 (and_7_out, ~decoder_1_out2, or_18_out);  // AND_Gate
  Shift_Register #(.length(4), .trigger("falling")) shift_register_1 (
    .shift(and_18_out), .in(nor_3_out), .clk(CLK_t), .load(nor_5_out), .clr(RESET_out), .d0(not_3_out),
    .q0(M1), .d1(and_7_out), .q1(shift_register_1_q1), .d2(1'b0), .q2(shift_register_1_q2), .d3(1'b0),
    .q3(shift_register_1_q3));  // open: out
  LED u_RD (.in(decoder_1_out6));
  or or_7 (or_7_out, multiplexer_5_out, and_6_out);
  Subtractor subtractor_1 (
    .a(multiplexer_15_out), .b(multiplexer_1_out), .out(subtractor_1_out), .bin(A0_q[1]),
    .bout(subtractor_1_bout));
  assign {nor_6_out[3], controlled_buffer_1_out_2, controlled_buffer_1_out} = decoder_1_out11 ? subtractor_1_out : 8'bz;  // Controlled_Buffer controlled_buffer_2
  and and_8 (and_8_out, decoder_1_out10, adder_1_cout);
  Shifter #(.shift("rr")) shifter_1 (.in(multiplexer_1_out), .\dist (counter_4_q[2:0]), .out(shifter_1_out));
  assign not_4_out = ~multiplexer_1_out;  // NOT_Gate not_4, 8 bits wide
  LED u_RAM (.in(RAM));
  nor nor_3 (nor_3_out, shift_register_1_q2, shift_register_1_q1, M1);
  nor nor_4 (RAM, shift_register_1_q1, M1);
  and and_9 (and_9_out, shift_register_1_q1, d_ff_2_q);
  and and_10 (and_10_out, shift_register_1_q2, decoder_1_out6);
  or or_8 (or_8_out[0], and_10_out, M1);
  and and_11 (or_8_out[1], shift_register_1_q2, decoder_1_out7[7]);
  or or_9 (or_9_out, shift_register_1_q3, shift_register_1_q2);
  and and_12 (and_12_out, or_9_out, decoder_1_out7[7]);
  or or_10 (or_10_out, shift_register_1_q3, not_2_out, shift_register_1_q1);
  and and_13 (and_13_out, shift_register_1_q1, ~or_17_out);  // AND_Gate
  or or_11 (or_11_out, and_13_out, or_12_out, or_5_out);
  D_Flip_Flop d_ff_1 (.clk(CLK_t), .D(or_7_out), .Qn(d_ff_1_qn), .en(shift_register_1_q1));  // open: Q, preset, reset
  and and_14 (and_14_out, or_18_out, d_ff_1_qn, shift_register_1_q1);
  assign and_15_out = multiplexer_15_out & multiplexer_2_out;  // AND_Gate and_15, 8 bits wide
  assign {nor_6_out[3], controlled_buffer_1_out_2, controlled_buffer_1_out} = decoder_1_out12 ? and_15_out : 8'bz;  // Controlled_Buffer controlled_buffer_3
  and and_16 (and_16_out, decoder_1_out11, subtractor_1_bout);
  Multiplexer #(.select(2), .width(8), .disabled(0), .enable("false")) multiplexer_2 (
    .in0(shifter_1_out), .in1(shifter_1_out), .in2(not_4_out),
    .in3({multiplexer_1_out[0], multiplexer_1_out[1], multiplexer_1_out[2], multiplexer_1_out[3], multiplexer_1_out[4], multiplexer_1_out[5], multiplexer_1_out[6], multiplexer_1_out[7]}),
    .out(multiplexer_2_out), .sel({counter_4_q[3], counter_4_q[0]}));
  or or_12 (or_12_out, decoder_1_out15, decoder_1_out14, decoder_1_out12, decoder_1_out13);
  LED READ (.in(RD));
  LED WRITE (.in(WR));
  not not_5 (not_5_out, decoder_1_out6);
  and and_17 (and_17_out, decoder_1_out6, shift_register_1_q3);
  nor nor_5 (nor_5_out, M1, decoder_1_out6, and_9_out, decoder_1_out7[7]);
  Register #(.width(2)) register_2 (.D(or_8_out), .Q({WR, RD}), .clk(CLK_t), .clr(RESET_out));  // open: en
  and and_18 (and_18_out, ~d_ff_2_q, or_10_out);  // AND_Gate
  Counter #(.width(16), .max('hffff)) IP (
    .load(and_5_out), .D(multiplexer_3_out), .count(and_19_out), .Q({IP_q_2, IP_q}), .clk(CLK_t),
    .clr(RESET_out));  // open: carry
  and and_19 (and_19_out, or_10_out, ~and_5_out, or_11_out);  // AND_Gate
  Multiplexer #(.width(16), .disabled(0), .enable("false")) multiplexer_3 (
    .in0({B0_q, C0_q_2, C0_q}), .in1({IC, counter_4_q, 4'b0000}), .out(multiplexer_3_out),
    .sel(decoder_1_out1));
  assign and_20_out = IC[7:4] & {4{nor_2_out[3]}};  // AND_Gate and_20, 4 bits wide
  or or_13 (or_13_out, decoder_1_out2, or_12_out, and_14_out);
  and and_21 (and_21_out, and_14_out, ~or_12_out, nor_2_out[3]);  // AND_Gate
  Clock clock_1 (.out(clock_1_out));
  Button TICK (.out(TICK_out));
  assign {nor_6_out[3], controlled_buffer_1_out_2, controlled_buffer_1_out} = decoder_1_out13 ? or_14_out : 8'bz;  // Controlled_Buffer controlled_buffer_4
  assign or_14_out = multiplexer_15_out | multiplexer_2_out;  // OR_Gate or_14, 8 bits wide
  or or_15 (nor_6_out[1], and_16_out, and_8_out);
  nor nor_6 (nor_6_out[0], controlled_buffer_1_out[0], controlled_buffer_1_out[1], controlled_buffer_1_out[2], controlled_buffer_1_out[3], controlled_buffer_1_out_2[0], controlled_buffer_1_out_2[1], controlled_buffer_1_out_2[2], nor_6_out[3]);
  or or_16 (or_16_out, not_5_out, and_17_out);
  assign DATA = and_12_out ? multiplexer_15_out : 8'bz;  // Controlled_Buffer controlled_buffer_5
  assign {nor_6_out[3], controlled_buffer_1_out_2, controlled_buffer_1_out} = decoder_1_out6 ? DATA : 8'bz;  // Controlled_Buffer controlled_buffer_6
  Counter #(.width(4), .max('hf)) counter_4 (
    .load(or_13_out), .D(and_20_out), .count(and_21_out), .Q(counter_4_q), .clk(CLK_t), .clr(RESET_out));  // open: carry
  Button RESET (.out(RESET_out));
  xor xor_1 (CLK_t, CLK, clock_1_out, TICK_out);
  Button u_BIT_4 (.out(BIT_4_out));
  Button u_BIT_5 (.out(BIT_5_out));
  Button u_BIT_6 (.out(BIT_6_out));
  Button u_BIT_7 (.out(BIT_7_out));
  assign {nor_6_out[3], controlled_buffer_1_out_2, controlled_buffer_1_out} = decoder_1_out14 ? xor_2_out : 8'bz;  // Controlled_Buffer controlled_buffer_7
  assign xor_2_out = multiplexer_15_out ^ multiplexer_2_out;  // XOR_Gate xor_2, 8 bits wide
  assign {nor_6_out[3], controlled_buffer_1_out_2, controlled_buffer_1_out} = decoder_1_out15 ? multiplexer_2_out : 8'bz;  // Controlled_Buffer controlled_buffer_8
  xor xor_3 (nor_6_out[2], controlled_buffer_1_out[0], controlled_buffer_1_out[1], controlled_buffer_1_out[2], controlled_buffer_1_out[3], controlled_buffer_1_out_2[0], controlled_buffer_1_out_2[1], controlled_buffer_1_out_2[2], nor_6_out[3]);
  LED led_1 (.in(A0_q[3]));
  LED led_2 (.in(A0_q_2[3]));
  LED led_3 (.in(A0_q[2]));
  LED led_4 (.in(A0_q_2[2]));
  LED led_5 (.in(A0_q_2[1]));
  LED led_6 (.in(A0_q_2[0]));
  Multiplexer #(.width(16), .disabled(0), .enable("false")) multiplexer_4 (
    .in0({IP_q_2, IP_q}), .in1(PTR), .out(ADDR), .sel(RAM));
  Register #(.trigger("falling")) u_IC (.D(DATA), .en(M1), .Q(IC), .clk(CLK_t), .clr(RESET_out));
  or or_17 (or_17_out, counter_4_q[1], counter_4_q[2], counter_4_q[3]);
  xor xor_4 (xor_4_out[0], BIT_4, BIT_4_out);
  xor xor_5 (xor_4_out[1], BIT_5, BIT_5_out);
  xor xor_6 (xor_4_out[2], BIT_6, BIT_6_out);
  xor xor_7 (xor_4_out[3], BIT_7, BIT_7_out);
  not not_6 (not_6_out, A0_q[2]);
  not not_7 (not_7_out, A0_q[3]);
  not not_8 (not_8_out, A0_q[1]);
  not not_9 (not_9_out, A0_q[0]);
  LED led_7 (.in(A0_q[1]));
  LED led_8 (.in(A0_q[0]));
  D_Flip_Flop d_ff_2 (.clk(CLK_t), .D(multiplexer_5_out), .Q(d_ff_2_q), .en(and_23_out));  // open: Qn, preset, reset
  and and_22 (and_22_out, d_ff_2_q, ~or_17_out);  // AND_Gate
  or or_18 (or_18_out, counter_4_q[0], or_17_out);
  // Probe on xor_4_out
  Multiplexer #(.select(3), .disabled(0)) multiplexer_5 (
    .in0(not_6_out), .in1(A0_q[2]), .in2(not_7_out), .in3(A0_q[3]), .in4(not_8_out), .in5(A0_q[1]),
    .in6(not_9_out), .in7(A0_q[0]), .out(multiplexer_5_out), .sel(IC[2:0]), .en(decoder_1_out8));
  nor nor_7 (nor_7_out, d_ff_2_q, M1);
  or or_19 (or_19_out, and_22_out, decoder_1_out8);
  and and_23 (and_23_out, or_19_out, nor_2_out[3]);
  RAM #(.addrWidth(16)) ram_2 (.addr(ADDR), .data(DATA), .clk(WR), .ld(RD));  // open: sel, clr
  // Probe on IC
  // Probe on {nor_6_out[3], controlled_buffer_1_out_2, controlled_buffer_1_out}
  or or_20 (or_20_out, IC[4], IC[5], IC[6], IC[7]);
  Decoder #(.select(2), .disabled(0)) decoder_2 (
    .out0(decoder_2_out0), .out1(decoder_2_out1), .out2(decoder_2_out2), .out3(decoder_2_out3),
    .sel(IC[5:4]), .en(decoder_1_out9));
  Decoder #(.select(2), .disabled(0)) decoder_3 (
    .out0(decoder_3_out0), .out1(decoder_3_out1), .out2(decoder_3_out2), .out3(decoder_3_out3),
    .sel(multiplexer_6_out), .en(or_2_out));
  Multiplexer #(.width(2), .disabled(0), .enable("false")) multiplexer_6 (
    .in0(R_T_2_q), .in1(IC[5:4]), .out(multiplexer_6_out), .sel(or_1_out));
  Register #(.width(4)) R_T_2 (
    .D({IC[5:4], IC[1:0]}), .en(decoder_1_out3), .Q({R_T_2_q, R_T_2_q_2}), .clk(CLK_t), .clr(RESET_out));
  Decoder #(.select(2), .disabled(0), .enable("false")) decoder_4 (
    .out1(decoder_4_out1), .sel(R_T_2_q_2));  // open: out0, out2, out3
  Multiplexer #(.width(2), .disabled(0), .enable("false")) multiplexer_7 (
    .in0(R_T_2_q), .in1(IC[5:4]), .out(multiplexer_7_out), .sel(or_1_out));
  nand nand_1 (nand_1_out, ~and_2_out, or_20_out);  // NAND_Gate
  and and_24 (and_24_out, decoder_3_out1, or_16_out);
  Hex_Digit_Display hex_digit_display_7 (.value(IC[7:4]));  // open: dp
  Hex_Digit_Display hex_digit_display_8 (.value(IC[3:0]));  // open: dp
  Register #(.width(4)) register_3 (.D(IC[3:0]), .en(decoder_2_out2), .Q(register_3_q), .clk(CLK_t), .clr(RESET_out));
  Decoder #(.select(4), .disabled(0), .enable("false")) decoder_5 (
    .out0(decoder_5_out0), .out1(decoder_5_out1), .out2(decoder_5_out2), .out3(decoder_5_out3),
    .out4(decoder_5_out4), .out5(decoder_5_out5), .out6(decoder_5_out6), .out7(decoder_5_out7),
    .out8(decoder_5_out8), .out9(decoder_5_out9), .sel(register_3_q));  // open: out10, out11, out12, out13, out14, out15
  Register #(.width(4)) register_4 (.D(IC[3:0]), .en(decoder_2_out3), .Q(register_4_q), .clk(CLK_t), .clr(RESET_out));
  Decoder #(.select(4), .disabled(0), .enable("false")) decoder_6 (
    .out0(decoder_6_out0), .out1(decoder_6_out1), .out2(decoder_6_out2), .out3(decoder_6_out3),
    .out4(decoder_6_out4), .out5(decoder_6_out5), .out6(decoder_6_out6), .out7(decoder_6_out7),
    .out8(decoder_6_out8), .out9(decoder_6_out9), .sel(register_4_q));  // open: out10, out11, out12, out13, out14, out15
  Register #(.width(4)) register_5 (.D(IC[3:0]), .en(decoder_2_out0), .Q(register_5_q), .clk(CLK_t), .clr(RESET_out));
  Decoder #(.select(4), .disabled(0), .enable("false")) decoder_7 (
    .out0(decoder_7_out0), .out1(decoder_7_out1), .out2(decoder_7_out2), .out3(decoder_7_out3),
    .out4(decoder_7_out4), .out5(decoder_7_out5), .out6(decoder_7_out6), .out7(decoder_7_out7),
    .out8(decoder_7_out8), .out9(decoder_7_out9), .sel(register_5_q));  // open: out10, out11, out12, out13, out14, out15
  Register #(.width(4)) register_6 (.D(IC[3:0]), .en(decoder_2_out1), .Q(register_6_q), .clk(CLK_t), .clr(RESET_out));
  Decoder #(.select(4), .disabled(0), .enable("false")) decoder_8 (
    .out0(decoder_8_out0), .out1(decoder_8_out1), .out2(decoder_8_out2), .out3(decoder_8_out3),
    .out4(decoder_8_out4), .out5(decoder_8_out5), .out6(decoder_8_out6), .out7(decoder_8_out7),
    .out8(decoder_8_out8), .out9(decoder_8_out9), .sel(register_6_q));  // open: out10, out11, out12, out13, out14, out15
  Hex_Digit_Display hex_digit_display_9 (.value(register_3_q));  // open: dp
  Multiplexer #(.width(4), .disabled(0), .enable("false")) multiplexer_8 (
    .in0(IC[7:4]), .in1(register_3_q), .out(multiplexer_8_out), .sel(or_1_out));
  Multiplexer #(.width(8), .disabled(0), .enable("false")) multiplexer_9 (
    .in0({nor_6_out[3], controlled_buffer_1_out_2, controlled_buffer_1_out}), .in1({xor_4_out, nor_6_out}),
    .out(multiplexer_9_out), .sel(or_4_out));
  Hex_Digit_Display hex_digit_display_10 (.value(register_4_q));  // open: dp
  Multiplexer #(.width(4), .disabled(0), .enable("false")) multiplexer_10 (
    .in0(IC[7:4]), .in1(register_4_q), .out(multiplexer_10_out), .sel(or_1_out));
  Multiplexer #(.width(8), .disabled(0), .enable("false")) multiplexer_11 (
    .in0({nor_6_out[3], controlled_buffer_1_out_2, controlled_buffer_1_out}), .in1(IP_q_2),
    .out(multiplexer_11_out), .sel(and_5_out));
  Hex_Digit_Display hex_digit_display_11 (.value(register_5_q));  // open: dp
  Multiplexer #(.width(4), .disabled(0), .enable("false")) multiplexer_12 (
    .in0(IC[7:4]), .in1(register_5_q), .out(multiplexer_12_out), .sel(or_1_out));
  Multiplexer #(.width(8), .disabled(0), .enable("false")) multiplexer_13 (
    .in0({nor_6_out[3], controlled_buffer_1_out_2, controlled_buffer_1_out}), .in1(IP_q),
    .out(multiplexer_13_out), .sel(and_5_out));
  Multiplexer #(.width(4), .disabled(0), .enable("false")) multiplexer_14 (
    .in0(IC[7:4]), .in1(register_6_q), .out(multiplexer_14_out), .sel(or_1_out));
  Hex_Digit_Display hex_digit_display_12 (.value(A0_q_2));  // open: dp
  assign {controlled_buffer_9_out_2, controlled_buffer_9_out} = decoder_5_out0 ? {A0_q_2, A0_q} : 8'bz;  // Controlled_Buffer controlled_buffer_9
  assign controlled_buffer_10_out = decoder_10_out0 ? {A0_q_2, A0_q} : 8'bz;  // Controlled_Buffer controlled_buffer_10
  Register A0 (.D(multiplexer_9_out), .en(or_21_out), .Q({A0_q_2, A0_q}), .clk(CLK_t), .clr(RESET_out));
  LED led_9 (.in(or_21_out));
  or or_21 (or_21_out, or_4_out, and_25_out);
  LED led_10 (.in(decoder_5_out0));
  and and_25 (and_25_out, decoder_5_out0, decoder_3_out2);
  LED led_11 (.in(decoder_10_out0));
  Hex_Digit_Display hex_digit_display_13 (.value(B0_q[7:4]));  // open: dp
  assign controlled_buffer_11_out = decoder_11_out0 ? B0_q : 8'bz;  // Controlled_Buffer controlled_buffer_11
  assign PTR[15:8] = decoder_6_out0 ? B0_q : 8'bz;  // Controlled_Buffer controlled_buffer_12
  Register B0 (.D(multiplexer_11_out), .en(or_22_out), .Q(B0_q), .clk(CLK_t), .clr(RESET_out));
  LED led_12 (.in(or_22_out));
  LED led_13 (.in(decoder_6_out0));
  or or_22 (or_22_out, and_5_out, and_26_out);
  and and_26 (and_26_out, decoder_6_out0, decoder_3_out3);
  LED led_14 (.in(decoder_11_out0));
  assign PTR[7:0] = decoder_7_out0 ? {C0_q_2, C0_q} : 8'bz;  // Controlled_Buffer controlled_buffer_13
  assign controlled_buffer_14_out = decoder_12_out0 ? {C0_q_2, C0_q} : 8'bz;  // Controlled_Buffer controlled_buffer_14
  Register C0 (.D(multiplexer_13_out), .en(or_23_out), .Q({C0_q_2, C0_q}), .clk(CLK_t), .clr(RESET_out));
  LED led_15 (.in(or_23_out));
  or or_23 (or_23_out, and_5_out, and_27_out);
  LED led_16 (.in(decoder_7_out0));
  and and_27 (and_27_out, decoder_7_out0, decoder_3_out0);
  LED led_17 (.in(decoder_12_out0));
  assign controlled_buffer_15_out = decoder_13_out0 ? undriven : 8'bz;  // Controlled_Buffer controlled_buffer_15
  assign controlled_buffer_16_out = decoder_8_out0 ? D0_q : 8'bz;  // Controlled_Buffer controlled_buffer_16
  Register D0 (
    .D({nor_6_out[3], controlled_buffer_1_out_2, controlled_buffer_1_out}), .en(and_28_out), .Q(D0_q),
    .clk(CLK_t), .clr(RESET_out));
  LED led_18 (.in(and_28_out));
  LED led_19 (.in(decoder_8_out0));
  and and_28 (and_28_out, decoder_8_out0, and_24_out);
  LED led_20 (.in(decoder_13_out0));
  and and_29 (and_29_out, decoder_13_out0, decoder_4_out1, shift_register_1_q1);
  Hex_Digit_Display hex_digit_display_14 (.value(A0_q));  // open: dp
  assign {controlled_buffer_9_out_2, controlled_buffer_9_out} = decoder_5_out1 ? A1_q : 8'bz;  // Controlled_Buffer controlled_buffer_17
  Register A1 (
    .D({nor_6_out[3], controlled_buffer_1_out_2, controlled_buffer_1_out}), .en(and_30_out), .Q(A1_q),
    .clk(CLK_t), .clr(RESET_out));
  LED led_21 (.in(and_30_out));
  and and_30 (and_30_out, decoder_5_out1, decoder_3_out2);
  Hex_Digit_Display hex_digit_display_15 (.value(B0_q[3:0]));  // open: dp
  Hex_Digit_Display hex_digit_display_16 (.value(C0_q_2));  // open: dp
  assign PTR[15:8] = decoder_6_out1 ? B1_q : 8'bz;  // Controlled_Buffer controlled_buffer_18
  Register B1 (
    .D({nor_6_out[3], controlled_buffer_1_out_2, controlled_buffer_1_out}), .en(and_31_out), .Q(B1_q),
    .clk(CLK_t), .clr(RESET_out));
  LED led_22 (.in(and_31_out));
  and and_31 (and_31_out, decoder_6_out1, decoder_3_out3);
  assign PTR[7:0] = decoder_7_out1 ? C1_q : 8'bz;  // Controlled_Buffer controlled_buffer_19
  Register C1 (
    .D({nor_6_out[3], controlled_buffer_1_out_2, controlled_buffer_1_out}), .en(and_32_out), .Q(C1_q),
    .clk(CLK_t), .clr(RESET_out));
  LED led_23 (.in(and_32_out));
  and and_32 (and_32_out, decoder_7_out1, decoder_3_out0);
  assign controlled_buffer_16_out = decoder_8_out1 ? D1_q : 8'bz;  // Controlled_Buffer controlled_buffer_20
  Register D1 (
    .D({nor_6_out[3], controlled_buffer_1_out_2, controlled_buffer_1_out}), .en(and_33_out), .Q(D1_q),
    .clk(CLK_t), .clr(RESET_out));
  LED led_24 (.in(and_33_out));
  and and_33 (and_33_out, decoder_8_out1, and_24_out);
  assign controlled_buffer_10_out = decoder_10_out1 ? A1_q : 8'bz;  // Controlled_Buffer controlled_buffer_21
  Register A2 (
    .D({nor_6_out[3], controlled_buffer_1_out_2, controlled_buffer_1_out}), .en(and_34_out), .Q(A2_q),
    .clk(CLK_t), .clr(RESET_out));
  LED led_25 (.in(decoder_5_out1));
  and and_34 (and_34_out, decoder_5_out2, decoder_3_out2);
  LED led_26 (.in(decoder_10_out1));
  Hex_Digit_Display hex_digit_display_17 (.value(C0_q));  // open: dp
  assign controlled_buffer_11_out = decoder_11_out1 ? B1_q : 8'bz;  // Controlled_Buffer controlled_buffer_22
  Register B2 (
    .D({nor_6_out[3], controlled_buffer_1_out_2, controlled_buffer_1_out}), .en(and_35_out), .Q(B2_q),
    .clk(CLK_t), .clr(RESET_out));
  LED led_27 (.in(decoder_6_out1));
  and and_35 (and_35_out, decoder_6_out2, decoder_3_out3);
  LED led_28 (.in(decoder_11_out1));
  assign controlled_buffer_14_out = decoder_12_out1 ? C1_q : 8'bz;  // Controlled_Buffer controlled_buffer_23
  Register C2 (
    .D({nor_6_out[3], controlled_buffer_1_out_2, controlled_buffer_1_out}), .en(and_36_out), .Q(C2_q),
    .clk(CLK_t), .clr(RESET_out));
  LED led_29 (.in(decoder_7_out1));
  and and_36 (and_36_out, decoder_7_out2, decoder_3_out0);
  LED led_30 (.in(decoder_12_out1));
  assign controlled_buffer_15_out = decoder_13_out1 ? undriven_2 : 8'bz;  // Controlled_Buffer controlled_buffer_24
  LED led_31 (.in(decoder_8_out1));
  LED led_32 (.in(decoder_13_out1));
  assign controlled_buffer_10_out = decoder_10_out2 ? A2_q : 8'bz;  // Controlled_Buffer controlled_buffer_25
  assign {controlled_buffer_9_out_2, controlled_buffer_9_out} = decoder_5_out2 ? A2_q : 8'bz;  // Controlled_Buffer controlled_buffer_26
  LED led_33 (.in(and_34_out));
  LED led_34 (.in(decoder_5_out2));
  LED led_35 (.in(decoder_10_out2));
  assign controlled_buffer_11_out = decoder_11_out2 ? B2_q : 8'bz;  // Controlled_Buffer controlled_buffer_27
  assign PTR[15:8] = decoder_6_out2 ? B2_q : 8'bz;  // Controlled_Buffer controlled_buffer_28
  LED led_36 (.in(and_35_out));
  LED led_37 (.in(decoder_6_out2));
  LED led_38 (.in(decoder_11_out2));
  assign PTR[7:0] = decoder_7_out2 ? C2_q : 8'bz;  // Controlled_Buffer controlled_buffer_29
  assign controlled_buffer_14_out = decoder_12_out2 ? C2_q : 8'bz;  // Controlled_Buffer controlled_buffer_30
  LED led_39 (.in(and_36_out));
  LED led_40 (.in(decoder_7_out2));
  LED led_41 (.in(decoder_12_out2));
  assign {controlled_buffer_9_out_2, controlled_buffer_9_out} = decoder_5_out3 ? A3_q : 8'bz;  // Controlled_Buffer controlled_buffer_31
  assign controlled_buffer_10_out = decoder_10_out3 ? A3_q : 8'bz;  // Controlled_Buffer controlled_buffer_32
  Register A3 (
    .D({nor_6_out[3], controlled_buffer_1_out_2, controlled_buffer_1_out}), .en(and_37_out), .Q(A3_q),
    .clk(CLK_t), .clr(RESET_out));
  LED led_42 (.in(and_37_out));
  LED led_43 (.in(decoder_5_out3));
  and and_37 (and_37_out, decoder_5_out3, decoder_3_out2);
  LED led_44 (.in(decoder_10_out3));
  assign controlled_buffer_11_out = decoder_11_out3 ? B3_q : 8'bz;  // Controlled_Buffer controlled_buffer_33
  assign PTR[15:8] = decoder_6_out3 ? B3_q : 8'bz;  // Controlled_Buffer controlled_buffer_34
  Register B3 (
    .D({nor_6_out[3], controlled_buffer_1_out_2, controlled_buffer_1_out}), .en(and_38_out), .Q(B3_q),
    .clk(CLK_t), .clr(RESET_out));
  LED led_45 (.in(and_38_out));
  LED led_46 (.in(decoder_6_out3));
  and and_38 (and_38_out, decoder_6_out3, decoder_3_out3);
  LED led_47 (.in(decoder_11_out3));
  assign controlled_buffer_14_out = decoder_12_out3 ? A3_2_q : 8'bz;  // Controlled_Buffer controlled_buffer_35
  assign PTR[7:0] = decoder_7_out3 ? A3_2_q : 8'bz;  // Controlled_Buffer controlled_buffer_36
  Register A3_2 (
    .D({nor_6_out[3], controlled_buffer_1_out_2, controlled_buffer_1_out}), .en(and_39_out), .Q(A3_2_q),
    .clk(CLK_t), .clr(RESET_out));
  LED led_48 (.in(and_39_out));
  LED led_49 (.in(decoder_7_out3));
  and and_39 (and_39_out, decoder_7_out3, decoder_3_out0);
  LED led_50 (.in(decoder_12_out3));
  assign {controlled_buffer_9_out_2, controlled_buffer_9_out} = decoder_5_out4 ? A4_q : 8'bz;  // Controlled_Buffer controlled_buffer_37
  assign controlled_buffer_10_out = decoder_10_out4 ? A4_q : 8'bz;  // Controlled_Buffer controlled_buffer_38
  Register A4 (
    .D({nor_6_out[3], controlled_buffer_1_out_2, controlled_buffer_1_out}), .en(and_40_out), .Q(A4_q),
    .clk(CLK_t), .clr(RESET_out));
  LED led_51 (.in(and_40_out));
  LED led_52 (.in(decoder_5_out4));
  and and_40 (and_40_out, decoder_5_out4, decoder_3_out2);
  LED led_53 (.in(decoder_10_out4));
  assign controlled_buffer_11_out = decoder_11_out4 ? B4_q : 8'bz;  // Controlled_Buffer controlled_buffer_39
  assign PTR[15:8] = decoder_6_out4 ? B4_q : 8'bz;  // Controlled_Buffer controlled_buffer_40
  Register B4 (
    .D({nor_6_out[3], controlled_buffer_1_out_2, controlled_buffer_1_out}), .en(and_41_out), .Q(B4_q),
    .clk(CLK_t), .clr(RESET_out));
  LED led_54 (.in(and_41_out));
  LED led_55 (.in(decoder_6_out4));
  and and_41 (and_41_out, decoder_6_out4, decoder_3_out3);
  LED led_56 (.in(decoder_11_out4));
  assign PTR[7:0] = decoder_7_out4 ? C4_q : 8'bz;  // Controlled_Buffer controlled_buffer_41
  assign controlled_buffer_14_out = decoder_12_out4 ? C4_q : 8'bz;  // Controlled_Buffer controlled_buffer_42
  Register C4 (
    .D({nor_6_out[3], controlled_buffer_1_out_2, controlled_buffer_1_out}), .en(and_42_out), .Q(C4_q),
    .clk(CLK_t), .clr(RESET_out));
  LED led_57 (.in(and_42_out));
  LED led_58 (.in(decoder_7_out4));
  and and_42 (and_42_out, decoder_7_out4, decoder_3_out0);
  LED led_59 (.in(decoder_12_out4));
  assign {controlled_buffer_9_out_2, controlled_buffer_9_out} = decoder_5_out5 ? A5_q : 8'bz;  // Controlled_Buffer controlled_buffer_43
  Register A5 (
    .D({nor_6_out[3], controlled_buffer_1_out_2, controlled_buffer_1_out}), .en(and_43_out), .Q(A5_q),
    .clk(CLK_t), .clr(RESET_out));
  LED led_60 (.in(and_43_out));
  and and_43 (and_43_out, decoder_5_out5, decoder_3_out2);
  assign PTR[15:8] = decoder_6_out5 ? B5_q : 8'bz;  // Controlled_Buffer controlled_buffer_44
  Register B5 (
    .D({nor_6_out[3], controlled_buffer_1_out_2, controlled_buffer_1_out}), .en(and_44_out), .Q(B5_q),
    .clk(CLK_t), .clr(RESET_out));
  LED led_61 (.in(and_44_out));
  and and_44 (and_44_out, decoder_6_out5, decoder_3_out3);
  assign PTR[7:0] = decoder_7_out5 ? C5_q : 8'bz;  // Controlled_Buffer controlled_buffer_45
  Register C5 (
    .D({nor_6_out[3], controlled_buffer_1_out_2, controlled_buffer_1_out}), .en(and_45_out), .Q(C5_q),
    .clk(CLK_t), .clr(RESET_out));
  LED led_62 (.in(and_45_out));
  and and_45 (and_45_out, decoder_7_out5, decoder_3_out0);
  Hex_Digit_Display hex_digit_display_18 (.value({nor_6_out[3], controlled_buffer_1_out_2}));  // open: dp
  assign controlled_buffer_10_out = decoder_10_out5 ? A5_q : 8'bz;  // Controlled_Buffer controlled_buffer_46
  Register A6 (
    .D({nor_6_out[3], controlled_buffer_1_out_2, controlled_buffer_1_out}), .en(and_46_out), .Q(A6_q),
    .clk(CLK_t), .clr(RESET_out));
  LED led_63 (.in(decoder_5_out5));
  and and_46 (and_46_out, decoder_5_out6, decoder_3_out2);
  LED led_64 (.in(decoder_10_out5));
  Hex_Digit_Display hex_digit_display_19 (.value({nor_6_out[3], controlled_buffer_1_out_2}));  // open: dp
  assign controlled_buffer_11_out = decoder_11_out5 ? B5_q : 8'bz;  // Controlled_Buffer controlled_buffer_47
  Register B6 (
    .D({nor_6_out[3], controlled_buffer_1_out_2, controlled_buffer_1_out}), .en(and_47_out), .Q(B6_q),
    .clk(CLK_t), .clr(RESET_out));
  LED led_65 (.in(decoder_6_out5));
  and and_47 (and_47_out, decoder_6_out6, decoder_3_out3);
  LED led_66 (.in(decoder_11_out5));
  Hex_Digit_Display hex_digit_display_20 (.value({nor_6_out[3], controlled_buffer_1_out_2}));  // open: dp
  assign controlled_buffer_14_out = decoder_12_out5 ? C5_q : 8'bz;  // Controlled_Buffer controlled_buffer_48
  Register C6 (
    .D({nor_6_out[3], controlled_buffer_1_out_2, controlled_buffer_1_out}), .en(and_48_out), .Q(C6_q),
    .clk(CLK_t), .clr(RESET_out));
  LED led_67 (.in(decoder_7_out5));
  and and_48 (and_48_out, decoder_7_out6, decoder_3_out0);
  LED led_68 (.in(decoder_12_out5));
  Hex_Digit_Display hex_digit_display_21 (.value(controlled_buffer_1_out));  // open: dp
  assign {controlled_buffer_9_out_2, controlled_buffer_9_out} = decoder_5_out6 ? A6_q : 8'bz;  // Controlled_Buffer controlled_buffer_49
  assign controlled_buffer_10_out = decoder_10_out6 ? A6_q : 8'bz;  // Controlled_Buffer controlled_buffer_50
  LED led_69 (.in(and_46_out));
  LED led_70 (.in(decoder_5_out6));
  LED led_71 (.in(decoder_10_out6));
  Hex_Digit_Display hex_digit_display_22 (.value(controlled_buffer_1_out));  // open: dp
  assign controlled_buffer_11_out = decoder_11_out6 ? B6_q : 8'bz;  // Controlled_Buffer controlled_buffer_51
  assign PTR[15:8] = decoder_6_out6 ? B6_q : 8'bz;  // Controlled_Buffer controlled_buffer_52
  LED led_72 (.in(and_47_out));
  LED led_73 (.in(decoder_6_out6));
  LED led_74 (.in(decoder_11_out6));
  Hex_Digit_Display hex_digit_display_23 (.value(controlled_buffer_1_out));  // open: dp
  assign controlled_buffer_14_out = decoder_12_out6 ? C6_q : 8'bz;  // Controlled_Buffer controlled_buffer_53
  assign PTR[7:0] = decoder_7_out6 ? C6_q : 8'bz;  // Controlled_Buffer controlled_buffer_54
  LED led_75 (.in(and_48_out));
  LED led_76 (.in(decoder_7_out6));
  LED led_77 (.in(decoder_12_out6));
  Hex_Digit_Display hex_digit_display_24 (.value(controlled_buffer_9_out_2));  // open: dp
  assign controlled_buffer_10_out = decoder_10_out7 ? A7_q : 8'bz;  // Controlled_Buffer controlled_buffer_55
  assign {controlled_buffer_9_out_2, controlled_buffer_9_out} = decoder_5_out7 ? A7_q : 8'bz;  // Controlled_Buffer controlled_buffer_56
  Register A7 (
    .D({nor_6_out[3], controlled_buffer_1_out_2, controlled_buffer_1_out}), .en(and_49_out), .Q(A7_q),
    .clk(CLK_t), .clr(RESET_out));
  LED led_78 (.in(and_49_out));
  LED led_79 (.in(decoder_5_out7));
  and and_49 (and_49_out, decoder_5_out7, decoder_3_out2);
  LED led_80 (.in(decoder_10_out7));
  Hex_Digit_Display hex_digit_display_25 (.value(PTR[15:12]));  // open: dp
  assign controlled_buffer_11_out = decoder_11_out7 ? B7_q : 8'bz;  // Controlled_Buffer controlled_buffer_57
  assign PTR[15:8] = decoder_6_out7 ? B7_q : 8'bz;  // Controlled_Buffer controlled_buffer_58
  Register B7 (
    .D({nor_6_out[3], controlled_buffer_1_out_2, controlled_buffer_1_out}), .en(and_50_out), .Q(B7_q),
    .clk(CLK_t), .clr(RESET_out));
  LED led_81 (.in(and_50_out));
  LED led_82 (.in(decoder_6_out7));
  and and_50 (and_50_out, decoder_6_out7, decoder_3_out3);
  LED led_83 (.in(decoder_11_out7));
  Hex_Digit_Display hex_digit_display_26 (.value(PTR[7:4]));  // open: dp
  assign PTR[7:0] = decoder_7_out7 ? C7_q : 8'bz;  // Controlled_Buffer controlled_buffer_59
  assign controlled_buffer_14_out = decoder_12_out7 ? C7_q : 8'bz;  // Controlled_Buffer controlled_buffer_60
  Register C7 (
    .D({nor_6_out[3], controlled_buffer_1_out_2, controlled_buffer_1_out}), .en(and_51_out), .Q(C7_q),
    .clk(CLK_t), .clr(RESET_out));
  LED led_84 (.in(and_51_out));
  LED led_85 (.in(decoder_7_out7));
  and and_51 (and_51_out, decoder_7_out7, decoder_3_out0);
  LED led_86 (.in(decoder_12_out7));
  Keyboard keyboard_1 (
    .clk(CLK_t), .re(and_56_out), .clr(RESET_out), .avail(keyboard_1_avail), .data(keyboard_1_data[6:0]));
  TTY tty_1 (
    .data({controlled_buffer_1_out_2, controlled_buffer_1_out}), .clk(CLK_t), .we(and_55_out), .clr(RESET_out));
  Hex_Digit_Display hex_digit_display_27 (.value(controlled_buffer_9_out));  // open: dp
  assign {controlled_buffer_9_out_2, controlled_buffer_9_out} = decoder_5_out8 ? A8_q : 8'bz;  // Controlled_Buffer controlled_buffer_61
  assign controlled_buffer_10_out = decoder_10_out8 ? A8_q : 8'bz;  // Controlled_Buffer controlled_buffer_62
  Register A8 (
    .D({nor_6_out[3], controlled_buffer_1_out_2, controlled_buffer_1_out}), .en(and_52_out), .Q(A8_q),
    .clk(CLK_t), .clr(RESET_out));
  LED led_87 (.in(and_52_out));
  LED led_88 (.in(decoder_5_out8));
  and and_52 (and_52_out, decoder_5_out8, decoder_3_out2);
  LED led_89 (.in(decoder_10_out8));
  Hex_Digit_Display hex_digit_display_28 (.value(PTR[11:8]));  // open: dp
  assign PTR[15:8] = decoder_6_out8 ? B8_q : 8'bz;  // Controlled_Buffer controlled_buffer_63
  assign controlled_buffer_11_out = decoder_11_out8 ? B8_q : 8'bz;  // Controlled_Buffer controlled_buffer_64
  Register B8 (
    .D({nor_6_out[3], controlled_buffer_1_out_2, controlled_buffer_1_out}), .en(and_53_out), .Q(B8_q),
    .clk(CLK_t), .clr(RESET_out));
  LED led_90 (.in(and_53_out));
  LED led_91 (.in(decoder_6_out8));
  and and_53 (and_53_out, decoder_6_out8, decoder_3_out3);
  LED led_92 (.in(decoder_11_out8));
  Hex_Digit_Display hex_digit_display_29 (.value(PTR[3:0]));  // open: dp
  assign PTR[7:0] = decoder_7_out8 ? C8_q : 8'bz;  // Controlled_Buffer controlled_buffer_65
  assign controlled_buffer_14_out = decoder_12_out8 ? C8_q : 8'bz;  // Controlled_Buffer controlled_buffer_66
  Register C8 (
    .D({nor_6_out[3], controlled_buffer_1_out_2, controlled_buffer_1_out}), .en(and_54_out), .Q(C8_q),
    .clk(CLK_t), .clr(RESET_out));
  LED led_93 (.in(and_54_out));
  LED led_94 (.in(decoder_7_out8));
  and and_54 (and_54_out, decoder_7_out8, decoder_3_out0);
  LED led_95 (.in(decoder_12_out8));
  assign controlled_buffer_15_out = decoder_13_out8 ? keyboard_1_data : 8'bz;  // Controlled_Buffer controlled_buffer_67
  assign controlled_buffer_16_out = decoder_8_out8 ? D8_q : 8'bz;  // Controlled_Buffer controlled_buffer_68
  Register D8 (
    .D({nor_6_out[3], controlled_buffer_1_out_2, controlled_buffer_1_out}), .en(and_55_out), .Q(D8_q),
    .clk(CLK_t), .clr(RESET_out));
  LED led_96 (.in(and_55_out));
  LED led_97 (.in(decoder_8_out8));
  and and_55 (and_55_out, decoder_8_out8, and_24_out);
  LED led_98 (.in(decoder_13_out8));
  and and_56 (and_56_out, decoder_13_out8, decoder_4_out1, shift_register_1_q1);
  Hex_Digit_Display hex_digit_display_30 (.value(controlled_buffer_10_out[3:0]));  // open: dp
  Hex_Digit_Display hex_digit_display_31 (.value(controlled_buffer_10_out[7:4]));  // open: dp
  assign {controlled_buffer_9_out_2, controlled_buffer_9_out} = decoder_5_out9 ? A9_q : 8'bz;  // Controlled_Buffer controlled_buffer_69
  Register A9 (
    .D({nor_6_out[3], controlled_buffer_1_out_2, controlled_buffer_1_out}), .en(and_57_out), .Q(A9_q),
    .clk(CLK_t), .clr(RESET_out));
  LED led_99 (.in(and_57_out));
  and and_57 (and_57_out, decoder_5_out9, decoder_3_out2);
  Hex_Digit_Display hex_digit_display_32 (.value(controlled_buffer_11_out[7:4]));  // open: dp
  Hex_Digit_Display hex_digit_display_33 (.value(controlled_buffer_11_out[3:0]));  // open: dp
  assign PTR[15:8] = decoder_6_out9 ? B9_q : 8'bz;  // Controlled_Buffer controlled_buffer_70
  Register B9 (
    .D({nor_6_out[3], controlled_buffer_1_out_2, controlled_buffer_1_out}), .en(and_58_out), .Q(B9_q),
    .clk(CLK_t), .clr(RESET_out));
  LED led_100 (.in(and_58_out));
  and and_58 (and_58_out, decoder_6_out9, decoder_3_out3);
  Hex_Digit_Display hex_digit_display_34 (.value(controlled_buffer_14_out[3:0]));  // open: dp
  Hex_Digit_Display hex_digit_display_35 (.value(controlled_buffer_14_out[7:4]));  // open: dp
  assign PTR[7:0] = decoder_7_out9 ? C9_q : 8'bz;  // Controlled_Buffer controlled_buffer_71
  Register C9 (
    .D({nor_6_out[3], controlled_buffer_1_out_2, controlled_buffer_1_out}), .en(and_59_out), .Q(C9_q),
    .clk(CLK_t), .clr(RESET_out));
  LED led_101 (.in(and_59_out));
  and and_59 (and_59_out, decoder_7_out9, decoder_3_out0);
  assign controlled_buffer_16_out = decoder_8_out9 ? D9_q : 8'bz;  // Controlled_Buffer controlled_buffer_72
  Register D9 (
    .D({nor_6_out[3], controlled_buffer_1_out_2, controlled_buffer_1_out}), .en(and_60_out), .Q(D9_q),
    .clk(CLK_t), .clr(RESET_out));
  LED led_102 (.in(and_60_out));
  and and_60 (and_60_out, decoder_8_out9, and_24_out);
  not not_10 (keyboard_1_data[7], keyboard_1_avail);
  Joystick joystick_1 (.x(joystick_1_x), .y(joystick_1_y));
  Hex_Digit_Display hex_digit_display_36 (.value(multiplexer_8_out));  // open: dp
  assign controlled_buffer_10_out = decoder_10_out9 ? A9_q : 8'bz;  // Controlled_Buffer controlled_buffer_73
  LED led_103 (.in(decoder_5_out9));
  LED led_104 (.in(decoder_10_out9));
  Hex_Digit_Display hex_digit_display_37 (.value(multiplexer_10_out));  // open: dp
  assign controlled_buffer_11_out = decoder_11_out9 ? B9_q : 8'bz;  // Controlled_Buffer controlled_buffer_74
  LED led_105 (.in(decoder_6_out9));
  LED led_106 (.in(decoder_11_out9));
  Hex_Digit_Display hex_digit_display_38 (.value(multiplexer_12_out));  // open: dp
  assign controlled_buffer_14_out = decoder_12_out9 ? C9_q : 8'bz;  // Controlled_Buffer controlled_buffer_75
  LED led_107 (.in(decoder_7_out9));
  LED led_108 (.in(decoder_12_out9));
  assign controlled_buffer_15_out = decoder_13_out9 ? {joystick_1_y, joystick_1_x} : 8'bz;  // Controlled_Buffer controlled_buffer_76
  LED led_109 (.in(decoder_8_out9));
  LED led_110 (.in(decoder_13_out9));
  DotMatrix #(.matrixcols(16), .matrixrows(1)) dotmatrix_1 (
    .col0(decoder_9_out0[0]), .col1(decoder_9_out0[1]), .col2(decoder_9_out0[2]), .col3(decoder_9_out0[3]),
    .col4(decoder_9_out0[4]), .col5(decoder_9_out0[5]), .col6(decoder_9_out0[6]), .col7(decoder_9_out0[7]),
    .col8(decoder_9_out0[8]), .col9(decoder_9_out0[9]), .col10(decoder_9_out0[10]),
    .col11(decoder_9_out0[11]), .col12(decoder_9_out0[12]), .col13(decoder_9_out0[13]),
    .col14(decoder_9_out0[14]), .col15(decoder_9_out0[15]));
  Decoder #(.select(4), .disabled(0), .enable("false")) decoder_9 (
    .out0(decoder_9_out0[0]), .out1(decoder_9_out0[1]), .out2(decoder_9_out0[2]), .out3(decoder_9_out0[3]),
    .out4(decoder_9_out0[4]), .out5(decoder_9_out0[5]), .out6(decoder_9_out0[6]), .out7(decoder_9_out0[7]),
    .out8(decoder_9_out0[8]), .out9(decoder_9_out0[9]), .out10(decoder_9_out0[10]),
    .out11(decoder_9_out0[11]), .out12(decoder_9_out0[12]), .out13(decoder_9_out0[13]),
    .out14(decoder_9_out0[14]), .out15(decoder_9_out0[15]), .sel(D9_q[3:0]));
  // DotMatrix #(.inputtype("select"), .matrixcols(4), .matrixrows(4)) dotmatrix_2: pin names not known; wires that end beside it: D9_q[3:0], D9_q[7:4]
  Decoder #(.select(4), .disabled(0), .enable("false")) decoder_10 (
    .out0(decoder_10_out0), .out1(decoder_10_out1), .out2(decoder_10_out2), .out3(decoder_10_out3),
    .out4(decoder_10_out4), .out5(decoder_10_out5), .out6(decoder_10_out6), .out7(decoder_10_out7),
    .out8(decoder_10_out8), .out9(decoder_10_out9), .sel(multiplexer_8_out));  // open: out10, out11, out12, out13, out14, out15
  Decoder #(.select(4), .disabled(0), .enable("false")) decoder_11 (
    .out0(decoder_11_out0), .out1(decoder_11_out1), .out2(decoder_11_out2), .out3(decoder_11_out3),
    .out4(decoder_11_out4), .out5(decoder_11_out5), .out6(decoder_11_out6), .out7(decoder_11_out7),
    .out8(decoder_11_out8), .out9(decoder_11_out9), .sel(multiplexer_10_out));  // open: out10, out11, out12, out13, out14, out15
  Decoder #(.select(4), .disabled(0), .enable("false")) decoder_12 (
    .out0(decoder_12_out0), .out1(decoder_12_out1), .out2(decoder_12_out2), .out3(decoder_12_out3),
    .out4(decoder_12_out4), .out5(decoder_12_out5), .out6(decoder_12_out6), .out7(decoder_12_out7),
    .out8(decoder_12_out8), .out9(decoder_12_out9), .sel(multiplexer_12_out));  // open: out10, out11, out12, out13, out14, out15
  assign and_61_out = controlled_buffer_16_out & {8{decoder_1_out7[7]}};  // AND_Gate and_61, 8 bits wide
  Decoder #(.select(4), .disabled(0), .enable("false")) decoder_13 (
    .out0(decoder_13_out0), .out1(decoder_13_out1), .out2(decoder_13_out2), .out3(decoder_13_out3),
    .out4(decoder_13_out4), .out5(decoder_13_out5), .out6(decoder_13_out6), .out7(decoder_13_out7),
    .out8(decoder_13_out8), .out9(decoder_13_out9), .sel(multiplexer_14_out));  // open: out10, out11, out12, out13, out14, out15
  Decoder #(.select(4), .disabled(0), .enable("false")) decoder_14 (
    .out0(decoder_14_out15[15]), .out1(decoder_14_out15[14]), .out2(decoder_14_out15[13]),
    .out3(decoder_14_out15[12]), .out4(decoder_14_out15[11]), .out5(decoder_14_out15[10]),
    .out6(decoder_14_out15[9]), .out7(decoder_14_out15[8]), .out8(decoder_14_out15[7]),
    .out9(decoder_14_out15[6]), .out10(decoder_14_out15[5]), .out11(decoder_14_out15[4]),
    .out12(decoder_14_out15[3]), .out13(decoder_14_out15[2]), .out14(decoder_14_out15[1]),
    .out15(decoder_14_out15[0]), .sel(D9_q[7:4]));
  Multiplexer #(.select(2), .width(8), .disabled(0), .enable("false")) multiplexer_15 (
    .in0(PTR[7:0]), .in1(and_61_out), .in2({controlled_buffer_9_out_2, controlled_buffer_9_out}),
    .in3(PTR[15:8]), .out(multiplexer_15_out), .sel(multiplexer_7_out));
  Multiplexer #(.select(2), .width(8), .disabled(0), .enable("false")) multiplexer_16 (
    .in0(controlled_buffer_14_out), .in1(controlled_buffer_15_out), .in2(controlled_buffer_10_out),
    .in3(controlled_buffer_11_out), .out(multiplexer_16_out), .sel(R_T_2_q_2));
  DotMatrix #(.matrixcols(1), .matrixrows(16)) dotmatrix_3 (.col0(decoder_14_out15));
  // DotMatrix #(.inputtype("select"), .matrixcols(16), .matrixrows(16), .persist(4096)) dotmatrix_4: pin names not known; wires that end beside it: decoder_9_out0, decoder_14_out15

  // Notes on the sheet:
  //   Koyaanisqatsi.rom
  //   contents of rom_1 (hex, n*v repeats v):
  //   71 1 2 3 4 5 6 7 8 9 7a 7b 7c 7d 7e 7f 72 b c d e f 10 11 12 13 7a 7b 7c 7d 7e 7f 72 15 16 17 18 19
  //   1a 1b 1c 1e 7a 7b 7c 7d 7e 7f 72 1f 20 21 22 23 24 25 26 27 7a 7b 7c 7d 7e 7f 72 29 2a 2b 2c 2d 2e
  //   2f 30 31 7a 7b 7c 7d 7e 7f 72 33 34 35 36 37 38 39 3a 3b 7a 7b 7c 7d 7e 7f 72 3d 3e 3f 40 41 42 43
  //   44 45 7a 7b 7c 7d 7e 7f 72 47 48 49 4a 4b 4c 4d 4e 4f 7a 7b 7c 7d 7e 7f 72 51 52 53 54 55 56 57 58
  //   59 7a 7b 7c 7d 7e 7f 72 5b 5c 5d 5e 5f 60 61 62 63 7a 7b 7c 7d 7e 7f 10*79 4*73 76 77 10*79 4*73 76
  //   77 10*79 4*73 76 77 10*79 4*73 76 77 70 7*71 8*78 16*71
  //   Current tick
  //   Total ticks
  //   FETCH
  //   ALU
  //   CASE
  //   Koyaanisqatsi.ram
  //   https://github.com/Alikberov/Koyaanisqatsi/
  //   REGISTERS FILE
  //   DEVICES FILE
endmodule
